# Fritzing sketch aqib (saved by Fritzing 0.9.3b)
breadboards: 1

parts:
  U1 = NodeMCU V3.0
  IC1 = MCP3008 8-channel 10-bit ADC [part_number=MCP3008]
  DHT1 = DHT22 Humidity and Temperature Sensor
  MQ131 = Gas Sensor Breakout Board
  MQ136 = Gas Sensor Breakout Board
  Nokia_5110_LCD_Module1 = Nokia 5110 LCD basado en PCD8544
  PMS5003 = rounded female alternating pin header, 8 pins [form="♀ (female rounded)"]
  MICS6814 = Generic female alternating header - 5 pins [form="♀ (female)" package=THT]

nets:
  N1: U1.D0, IC1.no_name_yet#13
  N2: U1.D1, Nokia_5110_LCD_Module1.CE
  N3: U1.D2, Nokia_5110_LCD_Module1.DC
  N4: U1.D3, Nokia_5110_LCD_Module1.DIN
  N5: U1.D4, Nokia_5110_LCD_Module1.CLK
  N6: U1.3V3, IC1.no_name_yet#15, IC1.no_name_yet#16
  N7: U1.GND#6, U1.D5, U1.GND#16, U1.GND#33, U1.SK, IC1.no_name_yet#9, IC1.no_name_yet#14, DHT1.DATA
  N8: U1.D6, IC1.no_name_yet#12
  N9: U1.D7, IC1.no_name_yet#11
  N10: U1.D8, IC1.no_name_yet#10
  N11: U1.RX, PMS5003.pin5
  N12: U1.TX, PMS5003.pin4
  N13: U1.S3, Nokia_5110_LCD_Module1.RST
  5V: U1.VU, DHT1.VDD, MQ131.5V, MQ136.5V, Nokia_5110_LCD_Module1.VCC, Nokia_5110_LCD_Module1.LIGHT, PMS5003.pin8, MICS6814.5V
  GND: U1.GND#41, U1.A0, DHT1.GND, MQ131.GND, MQ136.GND, Nokia_5110_LCD_Module1.GND, PMS5003.pin7, MICS6814.GND
  N14: IC1.no_name_yet#1, MICS6814.CO
  N15: IC1.no_name_yet#2, MICS6814.NH3
  N16: IC1.no_name_yet#3, MICS6814.NO2
  N17: IC1.no_name_yet#4, MQ136.AOUT
  N18: IC1.no_name_yet#5, MQ131.AOUT

custom parts:
  NodeMCU V3.0: ESP8266 based NodeMCU
  Gas Sensor Breakout Board: Gas sensor breakout board. Input voltage is 5V. Sensor output is available in analog and digital.
  Nokia 5110 LCD basado en PCD8544: Módulo Nokia 5110 LCD basado en el controlador PCD8544. Versión de 8 pines (sólo entrada).
  Generic female alternating header - 5 pins: Generic female alternating header
